# Fritzing sketch ground_station (saved by Fritzing 1.0.1rc)

parts:
  Raspberry_PI_Model_4B = Raspberry Pi 4B
  U1 = DRF1278F LoRa/FSK Module (SX1278, 433 MHz) [part_number=DRF1278F]
  ANT1 = Antenna

nets:
  3V3: Raspberry_PI_Model_4B.3V3, U1.VCC
  GND: Raspberry_PI_Model_4B.GND, U1.GND
  N1: Raspberry_PI_Model_4B.GPIO24, U1.DIO0
  N2: Raspberry_PI_Model_4B.GPIO10, U1.MOSI
  N3: Raspberry_PI_Model_4B.GPIO9, U1.MISO
  N4: Raspberry_PI_Model_4B.GPIO25, U1.RESET
  N5: Raspberry_PI_Model_4B.GPIO11, U1.SCK
  N6: U1.ANT, ANT1.antenna_lead

custom parts:
  DRF1278F LoRa/FSK Module (SX1278, 433 MHz): Dorji DRF1278F RF front-end module (Semtech SX1278), 17 x 17 mm, 15 castellated pads at 1.27 mm pitch, 1.8-3.6 V. Pin order from the DRF1278F datasheet Rev 1.1.
